# Fritzing sketch v1_alpha_test (saved by Fritzing 0.9.4)
breadboards: 1

parts:
  U1 = ESP8266 WiFi Module [part_number=ESP8266]
  LCM1602_IIC1 = LCM1602 IIC [part_number="LCM1602 IIC" chip_label="LCM1602 IIC" package="DIP (Dual Inline) [THT]"]
  U2 = LCD-16X2 [package=lcd-16x2_noholes]
  Componente2 = Arduino Uno (Rev3)
  R1 = Resistor [tolerance=±5% resistance=300 package=THT]
  LED1 = smd LED [color="Red (633nm)" package="0603 [SMD]"]

nets:
  VCC: U1.VCC, U1.CH_PD, Componente2.3V3
  N1: U1.GPIO_0, LCM1602_IIC1.SDA, Componente2.A4/SDA
  N2: U1.GPIO_2, LCM1602_IIC1.SCL, Componente2.A5/SCL
  GND: U1.GND, LCM1602_IIC1.GND, Componente2.GND, LED1.anode
  VSS: LCM1602_IIC1.VSS, U2.VSS
  VDD: LCM1602_IIC1.VDD, U2.VDD
  N3: LCM1602_IIC1.V0, U2.VO
  N4: LCM1602_IIC1.RS, U2.RS
  N5: LCM1602_IIC1.RW, U2.R_W
  N6: LCM1602_IIC1.E, U2.E
  N7: LCM1602_IIC1.D0, U2.DB0
  N8: LCM1602_IIC1.D1, U2.DB1
  N9: LCM1602_IIC1.D2, U2.DB2
  N10: LCM1602_IIC1.D3, U2.DB3
  N11: LCM1602_IIC1.D4, U2.DB4
  N12: LCM1602_IIC1.D5, U2.DB5
  N13: LCM1602_IIC1.D6, U2.DB6
  N14: LCM1602_IIC1.D7, U2.DB7
  N15: LCM1602_IIC1.A, U2.A
  N16: LCM1602_IIC1.K, U2.K
  VCC_2: LCM1602_IIC1.VCC, Componente2.5V
  N17: LCM1602_IIC1.LED_A, LCM1602_IIC1.LED_B
  N18: Componente2.D9_PWM, R1.Pin_1
  N19: R1.Pin_0, LED1.cathode

notes:
  3v3
  5v
  Cor dos cabos serial:
  Verde: SDA
  Amarelo: SCL

custom parts:
  ESP8266 WiFi Module: Generic WiFi Module based on the ESP8266 with onboard PCB antenna and UART communications
  LCM1602 IIC: I2C-Module to use a 1602 or 2004 LCD on with the wire.h libory Serial LCD Modul
